# Fritzing sketch LeseEuleV2_b (saved by Fritzing 0.9.10b)
circuit board: 4.38197cm x 5.62069cm
breadboards: 1

parts:
  MP3 = DFRobot DFPlayer Mini [part_number=DFR0299]
  PN532 = PN532 Elechouse RFID NFC Module V3
  Pause = Round Pushbutton
  UP = Round Pushbutton
  Down = Round Pushbutton
  Power = Pushbutton [package=THT]
  VCC1 = 4 x AAA Battery Mount
  LED4 = LED - 5mm [color="Red (633nm)" current=0.030 package="5 mm [THT]"]
  LED5 = LED - 5mm [color="Green (555nm)" current=0.030 package="5 mm [THT]"]
  LED6 = LED - 5mm [color="Green (555nm)" current=0.030 package="5 mm [THT]"]
  Pro_Mini = Arduino Pro Mini 35pin Clone (5V) (LeseEuleMod)
  100k = Resistor [tolerance=±5% power=0.25 resistance=100k package=THT]
  10k = Resistor [tolerance=±5% power=0.25 resistance=10k package=THT]
  10k_2 = Resistor [tolerance=±5% power=0.25 resistance=10k package=THT]
  MP3+ = PNP-Transistor [package="TO92 [THT]"]
  1k = Resistor [tolerance=±5% power=0.25W resistance=1k package=THT]
  D1 = Rectifier Diode [part_number=1N4001 package="300 mil [THT]"]
  10k_3 = Resistor [tolerance=±5% power=0.25 resistance=10k package=THT]
  100k_2 = Resistor [tolerance=±5% power=0.25 resistance=100k package=THT]
  LED+ = PNP-Transistor [package="TO92 [THT]"]
  NFC+ = PNP-Transistor [package="TO92 [THT]"]
  Buttons = double row male pin header, 6 pins [form="♂ (male)"]
  On/Off = molex pin header, 2 pins [form=molex]
  +/- = molex pin header, 2 pins [form=molex part_number="+ - " mpn="+ - " mn="+ - "]
  +_LED_- = male pin header, 6 pins [form="♂ (male)"]
  HeadPhone = male pin header, 6 pins [form="♂ (male)"]
  NFC = double row male pin header, 4 pins [form="♂ (male)"]

nets:
  N1: MP3.VCC, MP3+.E
  N2: MP3.RX, 1k.Pin_0
  N3: MP3.TX, Pro_Mini.pin29
  N4: MP3.DAC_R, HeadPhone.pin5
  N5: MP3.DAC_L, HeadPhone.pin4
  N6: MP3.SPK_1, HeadPhone.pin3
  N7: MP3.GND-1, MP3.GND-2, PN532.GND, Pause.leg1, UP.leg1, Down.leg1, VCC1.-, LED4.cathode, LED5.cathode, LED6.cathode, Pro_Mini.pin11, Pro_Mini.pin22, Buttons.pin4, Buttons.pin5, Buttons.pin6, +/-.pin2, +_LED_-.pin4, +_LED_-.pin5, +_LED_-.pin6, HeadPhone.pin2, NFC.pin4
  N8: MP3.SPK_2, HeadPhone.pin1
  N9: MP3.ADKEY_2, Pro_Mini.pin2
  N10: MP3.BUSY, Pro_Mini.pin28
  N11: PN532.VCC, NFC+.E, NFC.pin3
  N12: PN532.SDA, Pro_Mini.pin34, 10k_2.Pin_0, NFC.pin2
  N13: PN532.SCL, Pro_Mini.pin35, 10k.Pin_0, NFC.pin1
  N14: Pause.leg0, Pro_Mini.pin27, Buttons.pin1
  N15: UP.leg0, Pro_Mini.pin26, Buttons.pin2
  N16: Down.leg0, Pro_Mini.pin25, Buttons.pin3
  N17: Power.leg0, D1.cathode, On/Off.pin2
  N18: Power.leg1, Pro_Mini.pin9, 100k.Pin_1, 10k.Pin_1, 10k_2.Pin_1, MP3+.C, 100k_2.Pin_1, LED+.C, NFC+.C, On/Off.pin1
  N19: VCC1.+, D1.anode, +/-.pin1
  N20: LED4.anode, LED5.anode, LED6.anode, 100k.Pin_0, 10k_3.Pin_0, 100k_2.Pin_0, +_LED_-.pin1, +_LED_-.pin2, +_LED_-.pin3
  N21: Pro_Mini.pin3, MP3+.B, LED+.B
  N22: Pro_Mini.pin23, HeadPhone.pin6
  N23: Pro_Mini.pin24, NFC+.B
  N24: Pro_Mini.pin30, 1k.Pin_1
  N25: 10k_3.Pin_1, LED+.E

notes:
  Speaker
  DAC
  - +
  LeseEule 2.0

custom parts:
  PN532 Elechouse RFID NFC Module V3: NFC is a popular technology in recent years. We often heard this work while smart phone company such as Samsung or HTC introduces their latest high-end phones. Almost all the high-end phone in the market support NFC. Near field communication (NFC) is a set of standards for smart phones and similar devices to establish radio communication with each other by touching them together or bringing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
  Arduino Pro Mini 35pin Clone (5V) (LeseEuleMod): The Arduino Pro Mini is a microcontroller board based on the ATmega328 and originally produced by Sparkfun in two versions: 3.3V/8MHz and 5V/16MHz. The Pro Mini is an open hardware platform with variants made by several manufacturers. The present, 35-pin variant differs slightly from the original Pro Mini in that the A6 and A7 pins, together with an additional ground pin, have been moved to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
